# Fritzing sketch sname_camera (saved by Fritzing 0.9.3b)

parts:
  PWM1 = PCA9685 16x12-bit PWM Breakout
  Raspberry_Pi_1 = Raspberry Pi 3 [part_number=RPI-3-V1.2]
  J1 = Basic Servo
  J2 = Basic Servo
  VCC2 = 4 x AAA Battery Mount  # not connected
  U1 = TRANSCHIPTC5747 [package=camera_sfv24r-2st_2]  # not connected

nets:
  N1: PWM1.no_name_yet#0, J2.pulse
  N2: PWM1.no_name_yet#1, J1.pulse
  N3: PWM1.no_name_yet#100, PWM1.no_name_yet#101
  N4: PWM1.no_name_yet#601, PWM1.no_name_yet#1000, PWM1.no_name_yet#1001, Raspberry_Pi_1.GND
  N5: PWM1.no_name_yet#603, Raspberry_Pi_1.GPIO2
  N6: PWM1.no_name_yet#604, Raspberry_Pi_1.GPIO3
  N7: PWM1.no_name_yet#605, Raspberry_Pi_1.5V
